# Fritzing sketch UltrasonicRangeFinder2 (saved by Fritzing 0.9.3b)
breadboards: 1

parts:
  Part1 = Arduino Uno (Rev3)
  Part2 = SRF05 Ultrasonic Rangefinder
  LCD1 = LCD screen
  R1 = Rotary Potentiometer (Small) [maximum_resistance=100kΩ package=THT]

nets:
  N1: Part1.D8, LCD1.E
  N2: Part1.D9_PWM, LCD1.DB4
  N3: Part1.D10_PWM/SS, LCD1.DB5
  N4: Part1.D11_PWM/MOSI, LCD1.DB6
  N5: Part1.D12/MISO, LCD1.DB7
  GND: Part1.GND, Part2.GND, LCD1.VSS, LCD1.R/W, LCD1.LED-, R1.leg2
  N6: Part1.D4, Part2.Trig
  N7: Part1.D5_PWM, Part2.Echo
  N8: Part1.D7, LCD1.RS
  5V: Part1.5V, Part2.VCC, LCD1.VDD, LCD1.LED+, R1.leg1
  N9: LCD1.V0, R1.wiper

// code stored in the sketch: WarnerLibraryGolf.ino
/*
  WarnerLibraryGolf - Vote Display

 This sketch displays the vote count using a 20x4 LCD display.  


  The circuit:
 * LCD RS pin to digital pin 7
 * LCD Enable pin to digital pin 8
 * LCD D4 pin to digital pin 9
 * LCD D5 pin to digital pin 10
 * LCD D6 pin to digital pin 11
 * LCD D7 pin to digital pin 12
 * LCD R/W pin to ground
 * LCD VSS pin to ground
 * LCD VCC pin to 5V
 * 10K resistor:
 * ends to +5V and ground
 * wiper to LCD VO pin (pin 3)

 Library originally added 18 Apr 2008
 by David A. Mellis
 library modified 5 Jul 2009
 by Limor Fried (http://www.ladyada.net)
 example added 9 Jul 2009
 by Tom Igoe
 modified 22 Nov 2010
 by Tom Igoe
 modified 9 Sep 2016
 by Elijah Goodwin for Warner Library Haunted Mini-golf

 The example code for display is in the public domain.

 http://www.arduino.cc/en/Tutorial/LiquidCrystal
 */

// include the library code:
#include <LiquidCrystal.h>

//set up integer variables for vote counts and set to 0
int trumpCount = 0;
int clintonCount = 0;

// initialize the library with the numbers of the interface pins
LiquidCrystal lcd(7, 8, 9, 10, 11, 12);
#define trigPin 3
#define echoPin 2
#define trigPinT 4
#define echoPinT 5


void setup() {
  // set up the LCD's number of columns and rows:
  lcd.begin(20, 4);
  // set the pins for ultrasonic sensors
  pinMode(trigPin, OUTPUT);
  pinMode(echoPin, INPUT);
  pinMode(trigPinT, OUTPUT);
  pinMode(echoPinT, INPUT);
}

void loop() {
 // Print the candidate's names and vote count variables to the LCD
 lcd.setCursor(0, 0);
  //         --------------------
  lcd.print("Trump");
  // set the cursor to column 0, line 2
  // (note: line 2 is the third row, since counting begins with 0):
  lcd.setCursor(0, 2);
  //         --------------------
  lcd.print("Clinton");
  // set the cursor to column 0, line 1
  // (note: line 1 is the second row, since counting begins with 0):
  lcd.setCursor(0, 1);
  // print the vote count variable for Trump:
  lcd.print(trumpCount);
  // set the cursor to column 0, line 4
  // (note: line 1 is the second row, since counting begins with 0):
  lcd.setCursor(0, 3);
  // print the vote count variable for Clinton:
  lcd.print(clintonCount);
  //Ultrasonic Clinton vote count
  long duration, distance;
  digitalWrite(trigPin, LOW); 
  delayMicroseconds(2); 
  digitalWrite(trigPin, HIGH);
  delayMicroseconds(10); 
  digitalWrite(trigPin, LOW);
  duration = pulseIn(echoPin, HIGH);
  distance = (duration/2) / 2.91;
  //Ultrasonic Trump vote count
  long durationT, distanceT;
  digitalWrite(trigPinT, LOW); 
  delayMicroseconds(2); 
  digitalWrite(trigPinT, HIGH);
  delayMicroseconds(10); 
  digitalWrite(trigPinT, LOW);
  durationT = pulseIn(echoPinT, HIGH);
  distanceT = (durationT/2) / 2.91;
  if (distance < 80) {  // This is where the Clinton count variable is changed
    ++clintonCount;
    delay(500);
} else if (distanceT < 80) {  // This is where the Trump count variable is changed
    ++trumpCount;
    delay(500);
}
}
